# Fritzing sketch opstelling (saved by Fritzing 0.9.3b)

parts:
  Part9 = NRF24L01+ Breakout Board
  Part10 = NRF24L01+ Breakout Board
  Part11 = Arduino Nano (Rev3.0) (ICSP)
  Part12 = Arduino Nano (Rev3.0) (ICSP)
  Part13 = NRF24L01+ Breakout Board
  Part14 = NRF24L01+ Breakout Board
  Part15 = Arduino Nano (Rev3.0) (ICSP)
  Part16 = Arduino Nano (Rev3.0) (ICSP)

nets:
  GND: Part9.GND, Part11.VIN, Part11.GND, Part11.RESET
  VCC: Part9.VCC, Part11.AREF, Part11.3V3, Part11.D13/SCK
  N1: Part9.CE, Part11.D9
  N2: Part9.CS, Part11.D10
  N3: Part9.SCK, Part11.D8
  N4: Part9.MOSI, Part11.D5, Part11.D7
  N5: Part9.MISO, Part11.D4, Part11.D6
  GND_2: Part10.GND, Part12.VIN, Part12.GND, Part12.RESET
  VCC_2: Part10.VCC, Part12.AREF, Part12.3V3, Part12.D13/SCK
  N6: Part10.CE, Part12.D9
  N7: Part10.CS, Part12.D10, Part12.D11/MOSI
  N8: Part10.SCK, Part12.D8
  N9: Part10.MOSI, Part12.D7
  N10: Part10.MISO, Part12.D4, Part12.D6
  GND_3: Part13.GND, Part15.VIN, Part15.GND, Part15.RESET
  VCC_3: Part13.VCC, Part15.AREF, Part15.3V3, Part15.D13/SCK
  N11: Part13.CE, Part15.D9
  N12: Part13.CS, Part15.D10
  N13: Part13.SCK, Part15.D8
  N14: Part13.MOSI, Part15.D5, Part15.D7
  N15: Part13.MISO, Part15.D4, Part15.D6
  GND_4: Part14.GND, Part16.VIN, Part16.GND, Part16.RESET
  VCC_4: Part14.VCC, Part16.AREF, Part16.3V3, Part16.D13/SCK
  N16: Part14.CE, Part16.D9
  N17: Part14.CS, Part16.D10, Part16.D11/MOSI
  N18: Part14.SCK, Part16.D8
  N19: Part14.MOSI, Part16.D7
  N20: Part14.MISO, Part16.D4, Part16.D6
